// Logisim project regfile.circ as structural Verilog: 1 circuit, main circuit main
module main (
  input  [4:0] rs1,
  input  [4:0] rs2,
  input  [4:0] rd,
  input  [31:0] Write_Data,
  input  RegWEn,
  input  clk,
  output [31:0] ra,
  output [31:0] sp,
  output [31:0] t0,
  output [31:0] t1,
  output [31:0] t2,
  output [31:0] s0,
  output [31:0] s1,
  output [31:0] a0,
  output [31:0] Read_Data_1,
  output [31:0] Read_Data_2
);

  wire comparator_1_eq, comparator_2_eq, comparator_3_eq, comparator_4_eq, comparator_5_eq, comparator_6_eq,
       comparator_7_eq, comparator_8_eq, multiplexer_1_out, multiplexer_2_out, multiplexer_3_out,
       multiplexer_4_out, multiplexer_7_out, multiplexer_8_out, multiplexer_9_out, multiplexer_10_out;

  Comparator #(.width(5)) comparator_1 (.a(rd), .b(5'b00001), .eq(comparator_1_eq));  // open: gt, lt
  Comparator #(.width(5)) comparator_2 (.a(rd), .b(5'b00010), .eq(comparator_2_eq));  // open: gt, lt
  Comparator #(.width(5)) comparator_3 (.a(rd), .b(5'b00101), .eq(comparator_3_eq));  // open: gt, lt
  Comparator #(.width(5)) comparator_4 (.a(rd), .b(5'b00110), .eq(comparator_4_eq));  // open: gt, lt
  Multiplexer #(.enable("false")) multiplexer_1 (
    .in0(1'b0), .in1(RegWEn), .out(multiplexer_1_out), .sel(comparator_1_eq));
  Multiplexer #(.enable("false")) multiplexer_2 (
    .in0(1'b0), .in1(RegWEn), .out(multiplexer_2_out), .sel(comparator_2_eq));
  Multiplexer #(.enable("false")) multiplexer_3 (
    .in0(1'b0), .in1(RegWEn), .out(multiplexer_3_out), .sel(comparator_3_eq));
  Multiplexer #(.enable("false")) multiplexer_4 (
    .in0(1'b0), .in1(RegWEn), .out(multiplexer_4_out), .sel(comparator_4_eq));
  Multiplexer #(.select(5), .width(32), .enable("false")) multiplexer_5 (
    .in0({32{1'b0}}), .in1(ra), .in2(sp), .in5(t0), .in6(t1), .in7(t2), .in8(s0), .in9(s1), .in10(a0),
    .out(Read_Data_1), .sel(rs1));  // open: in3, in4, in11, in12, in13, in14, in15, in16, in17, in18, in19, in20, in21, in22, in23, in24, in25, in26, in27, in28, in29, in30, in31
  Register #(.width(32)) x1 (.D(Write_Data), .en(multiplexer_1_out), .clk(clk), .Q(ra));  // open: clr
  Register #(.width(32)) x2 (.D(Write_Data), .en(multiplexer_2_out), .clk(clk), .Q(sp));  // open: clr
  Register #(.width(32)) x5 (.D(Write_Data), .en(multiplexer_3_out), .clk(clk), .Q(t0));  // open: clr
  Register #(.width(32)) x6 (.D(Write_Data), .en(multiplexer_4_out), .clk(clk), .Q(t1));  // open: clr
  Multiplexer #(.select(5), .width(32), .enable("false")) multiplexer_6 (
    .in0({32{1'b0}}), .in1(ra), .in2(sp), .in5(t0), .in6(t1), .in7(t2), .in8(s0), .in9(s1), .in10(a0),
    .out(Read_Data_2), .sel(rs2));  // open: in3, in4, in11, in12, in13, in14, in15, in16, in17, in18, in19, in20, in21, in22, in23, in24, in25, in26, in27, in28, in29, in30, in31
  Comparator #(.width(5)) comparator_5 (.a(rd), .b(5'b00111), .eq(comparator_5_eq));  // open: gt, lt
  Comparator #(.width(5)) comparator_6 (.a(rd), .b(5'b01000), .eq(comparator_6_eq));  // open: gt, lt
  Comparator #(.width(5)) comparator_7 (.a(rd), .b(5'b01001), .eq(comparator_7_eq));  // open: gt, lt
  Comparator #(.width(5)) comparator_8 (.a(rd), .b(5'b01010), .eq(comparator_8_eq));  // open: gt, lt
  Multiplexer #(.enable("false")) multiplexer_7 (
    .in0(1'b0), .in1(RegWEn), .out(multiplexer_7_out), .sel(comparator_5_eq));
  Multiplexer #(.enable("false")) multiplexer_8 (
    .in0(1'b0), .in1(RegWEn), .out(multiplexer_8_out), .sel(comparator_6_eq));
  Multiplexer #(.enable("false")) multiplexer_9 (
    .in0(1'b0), .in1(RegWEn), .out(multiplexer_9_out), .sel(comparator_7_eq));
  Multiplexer #(.enable("false")) multiplexer_10 (
    .in0(1'b0), .in1(RegWEn), .out(multiplexer_10_out), .sel(comparator_8_eq));
  Register #(.width(32)) x7 (.D(Write_Data), .en(multiplexer_7_out), .clk(clk), .Q(t2));  // open: clr
  Register #(.width(32)) x8 (.D(Write_Data), .en(multiplexer_8_out), .clk(clk), .Q(s0));  // open: clr
  Register #(.width(32)) x9 (.D(Write_Data), .en(multiplexer_9_out), .clk(clk), .Q(s1));  // open: clr
  Register #(.width(32)) x10 (.D(Write_Data), .en(multiplexer_10_out), .clk(clk), .Q(a0));  // open: clr

  // Other names for the same wires on the sheet: read_data1[31:0] = Read_Data_1; read_data2[31:0] = Read_Data_2;
  //   read_reg1[4:0] = rs1; read_reg2[4:0] = rs2; write_en = RegWEn; write_reg[4:0] = rd

  // Notes on the sheet:
  //   INPUTS to your circuit
  //   DON'T CHANGE THE LOCATIONS OF THE INPUTS AND OUTPUTS!
  //   These are DEBUG/TEST outputs from your circuit.
  //   OUTPUTS from your circuit
endmodule
