// Logisim project alu.circ as structural Verilog: 1 circuit, main circuit alu
module alu (
  input  [31:0] A,
  input  [31:0] B,
  input  [3:0] ALUSel,
  output [31:0] Result
);

  wire adder_67_cout, comparator_1_lt, xor_2_out;
  wire [4:0] bit_extender_1_out, bit_extender_2_out, bit_extender_3_out;
  wire [31:0] add, adder_3_out, adder_4_out, adder_5_out, adder_6_out, adder_7_out, adder_8_out, adder_9_out,
       adder_10_out, adder_11_out, adder_12_out, adder_13_out, adder_14_out, adder_15_out, adder_16_out,
       adder_17_out, adder_18_out, adder_19_out, adder_20_out, adder_21_out, adder_22_out, adder_23_out,
       adder_24_out, adder_25_out, adder_26_out, adder_27_out, adder_28_out, adder_29_out, adder_30_out,
       adder_31_out, adder_32_out, adder_33_out, adder_34_out, adder_35_out, adder_36_out, adder_37_out,
       adder_38_out, adder_39_out, adder_40_out, adder_41_out, adder_42_out, adder_43_out, adder_44_out,
       adder_45_out, adder_46_out, adder_47_out, adder_48_out, adder_49_out, adder_50_out, adder_51_out,
       adder_52_out, adder_53_out, adder_54_out, adder_55_out, adder_56_out, adder_57_out, adder_58_out,
       adder_59_out, adder_60_out, adder_62_out, adder_63_out, adder_65_out, adder_66_out, adder_68_out,
       bit_extender_5_out, bit_extender_6_out, bit_extender_7_out, bit_extender_8_out, bit_extender_9_out,
       bit_extender_10_out, bit_extender_11_out, bit_extender_12_out, bit_extender_13_out,
       bit_extender_14_out, bit_extender_15_out, bit_extender_16_out, bit_extender_17_out,
       bit_extender_18_out, bit_extender_19_out, bit_extender_20_out, bit_extender_21_out,
       bit_extender_22_out, bit_extender_23_out, bit_extender_24_out, bit_extender_25_out,
       bit_extender_26_out, bit_extender_27_out, bit_extender_28_out, bit_extender_29_out,
       bit_extender_30_out, bit_extender_31_out, bit_extender_32_out, bit_extender_33_out,
       bit_extender_34_out, bit_extender_35_out, bit_extender_36_out, bit_extender_37_out,
       bit_extender_38_out, bit_extender_39_out, bit_extender_40_out, bit_extender_41_out,
       bit_extender_42_out, bit_extender_43_out, bit_extender_44_out, bit_extender_45_out,
       bit_extender_46_out, bit_extender_47_out, bit_extender_48_out, bit_extender_49_out,
       bit_extender_50_out, bit_extender_51_out, bit_extender_52_out, bit_extender_53_out,
       bit_extender_54_out, bit_extender_55_out, bit_extender_56_out, bit_extender_57_out,
       bit_extender_58_out, bit_extender_59_out, bit_extender_60_out, bit_extender_61_out,
       bit_extender_62_out, bit_extender_63_out, bit_extender_64_out, bit_extender_65_out,
       bit_extender_66_out, bit_extender_67_out, bit_extender_68_out, bit_extender_69_out, cnto1, divu, mulh,
       mulhu, mult, multiplexer_2_out, multiplexer_3_out, multiplier_1_out, multiplier_3_cout,
       multiplier_3_out, my_and, my_or, my_sll, my_slt, my_sra, my_srl, my_xor, not_1_out, not_2_out,
       not_3_out, ontoA, ontoB, remu, sub;

  Adder #(.width(32)) adder_1 (.a(A), .b(B), .out(add));  // open: cin, cout
  assign my_and = A & B;  // AND_Gate and_1, 32 bits wide
  assign my_or = A | B;  // OR_Gate or_1, 32 bits wide
  Subtractor #(.width(32)) subtractor_1 (.a(A), .b(B), .out(sub));  // open: bin, bout
  assign my_xor = A ^ B;  // XOR_Gate xor_1, 32 bits wide
  Adder #(.width(32)) adder_2 (.a(ontoA), .b(ontoB), .out(cnto1));  // open: cin, cout
  Bit_Extender #(.in_width(32), .out_width(5)) bit_extender_1 (.in(B), .out(bit_extender_1_out));
  Bit_Extender #(.in_width(32), .out_width(5)) bit_extender_2 (.in(B), .out(bit_extender_2_out));
  Bit_Extender #(.in_width(32), .out_width(5)) bit_extender_3 (.in(B), .out(bit_extender_3_out));
  Shifter #(.width(32), .shift("lr")) shifter_1 (.in(A), .\dist (bit_extender_1_out), .out(my_srl));
  Shifter #(.width(32), .shift("ar")) shifter_2 (.in(A), .\dist (bit_extender_2_out), .out(my_sra));
  Shifter #(.width(32)) shifter_3 (.in(A), .\dist (bit_extender_3_out), .out(my_sll));
  Comparator #(.width(32)) comparator_1 (.a(A), .b(B), .lt(comparator_1_lt));  // open: gt, eq
  assign my_slt = {{31{1'b0}}, comparator_1_lt};  // Bit_Extender bit_extender_4
  assign bit_extender_5_out = {{31{1'b0}}, B[0]};  // Bit_Extender bit_extender_5
  assign bit_extender_6_out = {{31{1'b0}}, B[1]};  // Bit_Extender bit_extender_6
  assign bit_extender_7_out = {{31{1'b0}}, B[2]};  // Bit_Extender bit_extender_7
  assign bit_extender_8_out = {{31{1'b0}}, B[3]};  // Bit_Extender bit_extender_8
  assign bit_extender_9_out = {{31{1'b0}}, B[4]};  // Bit_Extender bit_extender_9
  assign bit_extender_10_out = {{31{1'b0}}, B[5]};  // Bit_Extender bit_extender_10
  assign bit_extender_11_out = {{31{1'b0}}, B[6]};  // Bit_Extender bit_extender_11
  assign bit_extender_12_out = {{31{1'b0}}, B[7]};  // Bit_Extender bit_extender_12
  assign bit_extender_13_out = {{31{1'b0}}, B[9]};  // Bit_Extender bit_extender_13
  assign bit_extender_14_out = {{31{1'b0}}, B[8]};  // Bit_Extender bit_extender_14
  assign bit_extender_15_out = {{31{1'b0}}, B[12]};  // Bit_Extender bit_extender_15
  assign bit_extender_16_out = {{31{1'b0}}, B[13]};  // Bit_Extender bit_extender_16
  assign bit_extender_17_out = {{31{1'b0}}, B[14]};  // Bit_Extender bit_extender_17
  assign bit_extender_18_out = {{31{1'b0}}, B[11]};  // Bit_Extender bit_extender_18
  assign bit_extender_19_out = {{31{1'b0}}, B[10]};  // Bit_Extender bit_extender_19
  assign bit_extender_20_out = {{31{1'b0}}, B[15]};  // Bit_Extender bit_extender_20
  assign bit_extender_21_out = {{31{1'b0}}, B[30]};  // Bit_Extender bit_extender_21
  assign bit_extender_22_out = {{31{1'b0}}, B[22]};  // Bit_Extender bit_extender_22
  assign bit_extender_23_out = {{31{1'b0}}, B[25]};  // Bit_Extender bit_extender_23
  assign bit_extender_24_out = {{31{1'b0}}, B[27]};  // Bit_Extender bit_extender_24
  assign bit_extender_25_out = {{31{1'b0}}, B[24]};  // Bit_Extender bit_extender_25
  assign bit_extender_26_out = {{31{1'b0}}, B[20]};  // Bit_Extender bit_extender_26
  assign bit_extender_27_out = {{31{1'b0}}, B[26]};  // Bit_Extender bit_extender_27
  assign bit_extender_28_out = {{31{1'b0}}, B[16]};  // Bit_Extender bit_extender_28
  assign bit_extender_29_out = {{31{1'b0}}, B[17]};  // Bit_Extender bit_extender_29
  assign bit_extender_30_out = {{31{1'b0}}, B[28]};  // Bit_Extender bit_extender_30
  assign bit_extender_31_out = {{31{1'b0}}, B[29]};  // Bit_Extender bit_extender_31
  assign bit_extender_32_out = {{31{1'b0}}, B[23]};  // Bit_Extender bit_extender_32
  assign bit_extender_33_out = {{31{1'b0}}, B[19]};  // Bit_Extender bit_extender_33
  assign bit_extender_34_out = {{31{1'b0}}, B[21]};  // Bit_Extender bit_extender_34
  assign bit_extender_35_out = {{31{1'b0}}, B[31]};  // Bit_Extender bit_extender_35
  assign bit_extender_36_out = {{31{1'b0}}, B[18]};  // Bit_Extender bit_extender_36
  Adder #(.width(32)) adder_3 (.a(bit_extender_5_out), .b(bit_extender_6_out), .out(adder_3_out));  // open: cin, cout
  Adder #(.width(32)) adder_4 (.a(bit_extender_7_out), .b(bit_extender_8_out), .out(adder_4_out));  // open: cin, cout
  Adder #(.width(32)) adder_5 (.a(bit_extender_9_out), .b(bit_extender_10_out), .out(adder_5_out));  // open: cin, cout
  Adder #(.width(32)) adder_6 (.a(bit_extender_11_out), .b(bit_extender_12_out), .out(adder_6_out));  // open: cin, cout
  Adder #(.width(32)) adder_7 (.a(bit_extender_13_out), .b(bit_extender_14_out), .out(adder_7_out));  // open: cin, cout
  Adder #(.width(32)) adder_8 (.a(bit_extender_15_out), .b(bit_extender_16_out), .out(adder_8_out));  // open: cin, cout
  Adder #(.width(32)) adder_9 (.a(bit_extender_17_out), .b(bit_extender_18_out), .out(adder_9_out));  // open: cin, cout
  Adder #(.width(32)) adder_10 (
    .a(bit_extender_19_out), .b(bit_extender_20_out), .out(adder_10_out));  // open: cin, cout
  Adder #(.width(32)) adder_11 (
    .a(bit_extender_21_out), .b(bit_extender_22_out), .out(adder_11_out));  // open: cin, cout
  Adder #(.width(32)) adder_12 (
    .a(bit_extender_23_out), .b(bit_extender_24_out), .out(adder_12_out));  // open: cin, cout
  Adder #(.width(32)) adder_13 (
    .a(bit_extender_25_out), .b(bit_extender_26_out), .out(adder_13_out));  // open: cin, cout
  Adder #(.width(32)) adder_14 (
    .a(bit_extender_27_out), .b(bit_extender_28_out), .out(adder_14_out));  // open: cin, cout
  Adder #(.width(32)) adder_15 (
    .a(bit_extender_29_out), .b(bit_extender_30_out), .out(adder_15_out));  // open: cin, cout
  Adder #(.width(32)) adder_16 (
    .a(bit_extender_31_out), .b(bit_extender_32_out), .out(adder_16_out));  // open: cin, cout
  Adder #(.width(32)) adder_17 (
    .a(bit_extender_33_out), .b(bit_extender_34_out), .out(adder_17_out));  // open: cin, cout
  Adder #(.width(32)) adder_18 (
    .a(bit_extender_35_out), .b(bit_extender_36_out), .out(adder_18_out));  // open: cin, cout
  assign bit_extender_37_out = {{31{1'b0}}, A[0]};  // Bit_Extender bit_extender_37
  assign bit_extender_38_out = {{31{1'b0}}, A[1]};  // Bit_Extender bit_extender_38
  assign bit_extender_39_out = {{31{1'b0}}, A[2]};  // Bit_Extender bit_extender_39
  assign bit_extender_40_out = {{31{1'b0}}, A[3]};  // Bit_Extender bit_extender_40
  assign bit_extender_41_out = {{31{1'b0}}, A[4]};  // Bit_Extender bit_extender_41
  assign bit_extender_42_out = {{31{1'b0}}, A[5]};  // Bit_Extender bit_extender_42
  assign bit_extender_43_out = {{31{1'b0}}, A[6]};  // Bit_Extender bit_extender_43
  assign bit_extender_44_out = {{31{1'b0}}, A[7]};  // Bit_Extender bit_extender_44
  assign bit_extender_45_out = {{31{1'b0}}, A[9]};  // Bit_Extender bit_extender_45
  assign bit_extender_46_out = {{31{1'b0}}, A[8]};  // Bit_Extender bit_extender_46
  assign bit_extender_47_out = {{31{1'b0}}, A[12]};  // Bit_Extender bit_extender_47
  assign bit_extender_48_out = {{31{1'b0}}, A[13]};  // Bit_Extender bit_extender_48
  assign bit_extender_49_out = {{31{1'b0}}, A[14]};  // Bit_Extender bit_extender_49
  assign bit_extender_50_out = {{31{1'b0}}, A[11]};  // Bit_Extender bit_extender_50
  assign bit_extender_51_out = {{31{1'b0}}, A[10]};  // Bit_Extender bit_extender_51
  assign bit_extender_52_out = {{31{1'b0}}, A[15]};  // Bit_Extender bit_extender_52
  assign bit_extender_53_out = {{31{1'b0}}, A[30]};  // Bit_Extender bit_extender_53
  assign bit_extender_54_out = {{31{1'b0}}, A[22]};  // Bit_Extender bit_extender_54
  assign bit_extender_55_out = {{31{1'b0}}, A[25]};  // Bit_Extender bit_extender_55
  assign bit_extender_56_out = {{31{1'b0}}, A[27]};  // Bit_Extender bit_extender_56
  assign bit_extender_57_out = {{31{1'b0}}, A[24]};  // Bit_Extender bit_extender_57
  assign bit_extender_58_out = {{31{1'b0}}, A[20]};  // Bit_Extender bit_extender_58
  assign bit_extender_59_out = {{31{1'b0}}, A[26]};  // Bit_Extender bit_extender_59
  assign bit_extender_60_out = {{31{1'b0}}, A[16]};  // Bit_Extender bit_extender_60
  assign bit_extender_61_out = {{31{1'b0}}, A[17]};  // Bit_Extender bit_extender_61
  assign bit_extender_62_out = {{31{1'b0}}, A[28]};  // Bit_Extender bit_extender_62
  assign bit_extender_63_out = {{31{1'b0}}, A[29]};  // Bit_Extender bit_extender_63
  assign bit_extender_64_out = {{31{1'b0}}, A[23]};  // Bit_Extender bit_extender_64
  assign bit_extender_65_out = {{31{1'b0}}, A[19]};  // Bit_Extender bit_extender_65
  assign bit_extender_66_out = {{31{1'b0}}, A[21]};  // Bit_Extender bit_extender_66
  assign bit_extender_67_out = {{31{1'b0}}, A[31]};  // Bit_Extender bit_extender_67
  assign bit_extender_68_out = {{31{1'b0}}, A[18]};  // Bit_Extender bit_extender_68
  Adder #(.width(32)) adder_19 (.a(adder_3_out), .b(adder_4_out), .out(adder_19_out));  // open: cin, cout
  Adder #(.width(32)) adder_20 (.a(adder_5_out), .b(adder_6_out), .out(adder_20_out));  // open: cin, cout
  Adder #(.width(32)) adder_21 (.a(adder_7_out), .b(adder_8_out), .out(adder_21_out));  // open: cin, cout
  Adder #(.width(32)) adder_22 (.a(adder_9_out), .b(adder_10_out), .out(adder_22_out));  // open: cin, cout
  Adder #(.width(32)) adder_23 (.a(adder_11_out), .b(adder_12_out), .out(adder_23_out));  // open: cin, cout
  Adder #(.width(32)) adder_24 (.a(adder_13_out), .b(adder_14_out), .out(adder_24_out));  // open: cin, cout
  Adder #(.width(32)) adder_25 (.a(adder_15_out), .b(adder_16_out), .out(adder_25_out));  // open: cin, cout
  Adder #(.width(32)) adder_26 (.a(adder_17_out), .b(adder_18_out), .out(adder_26_out));  // open: cin, cout
  Divider #(.width(32)) divider_1 (.a(A), .b(B), .out(divu));  // open: upper, rem
  Multiplier #(.width(32)) multiplier_1 (.a(divu), .b(B), .out(multiplier_1_out));  // open: cin, cout
  Multiplier #(.width(32)) multiplier_2 (.a(A), .b(B), .out(mult), .cout(mulhu));  // open: cin
  Adder #(.width(32)) adder_27 (.a(adder_19_out), .b(adder_20_out), .out(adder_27_out));  // open: cin, cout
  Adder #(.width(32)) adder_28 (.a(adder_21_out), .b(adder_22_out), .out(adder_28_out));  // open: cin, cout
  Adder #(.width(32)) adder_29 (.a(adder_23_out), .b(adder_24_out), .out(adder_29_out));  // open: cin, cout
  Adder #(.width(32)) adder_30 (.a(adder_25_out), .b(adder_26_out), .out(adder_30_out));  // open: cin, cout
  Multiplexer #(.select(4), .width(32), .enable("false")) multiplexer_1 (
    .in0(add), .in1(my_and), .in2(my_or), .in3(my_xor), .in4(my_srl), .in5(my_sra), .in6(my_sll),
    .in7(my_slt), .in8(divu), .in9(remu), .in10(mult), .in11(mulhu), .in12(sub), .in13(cnto1), .in14(mulh),
    .out(Result), .sel(ALUSel));  // open: in15
  Subtractor #(.width(32)) subtractor_2 (.a(A), .b(multiplier_1_out), .out(remu));  // open: bin, bout
  Adder #(.width(32)) adder_31 (
    .a(bit_extender_37_out), .b(bit_extender_38_out), .out(adder_31_out));  // open: cin, cout
  Adder #(.width(32)) adder_32 (.a(adder_31_out), .b(adder_33_out), .out(adder_32_out));  // open: cin, cout
  Adder #(.width(32)) adder_33 (
    .a(bit_extender_39_out), .b(bit_extender_40_out), .out(adder_33_out));  // open: cin, cout
  Adder #(.width(32)) adder_34 (
    .a(bit_extender_41_out), .b(bit_extender_42_out), .out(adder_34_out));  // open: cin, cout
  Adder #(.width(32)) adder_35 (.a(adder_34_out), .b(adder_36_out), .out(adder_35_out));  // open: cin, cout
  Adder #(.width(32)) adder_36 (
    .a(bit_extender_43_out), .b(bit_extender_44_out), .out(adder_36_out));  // open: cin, cout
  Adder #(.width(32)) adder_37 (
    .a(bit_extender_45_out), .b(bit_extender_46_out), .out(adder_37_out));  // open: cin, cout
  Adder #(.width(32)) adder_38 (.a(adder_37_out), .b(adder_39_out), .out(adder_38_out));  // open: cin, cout
  Adder #(.width(32)) adder_39 (
    .a(bit_extender_47_out), .b(bit_extender_48_out), .out(adder_39_out));  // open: cin, cout
  Adder #(.width(32)) adder_40 (
    .a(bit_extender_49_out), .b(bit_extender_50_out), .out(adder_40_out));  // open: cin, cout
  Adder #(.width(32)) adder_41 (.a(adder_40_out), .b(adder_42_out), .out(adder_41_out));  // open: cin, cout
  Adder #(.width(32)) adder_42 (
    .a(bit_extender_51_out), .b(bit_extender_52_out), .out(adder_42_out));  // open: cin, cout
  Adder #(.width(32)) adder_43 (
    .a(bit_extender_53_out), .b(bit_extender_54_out), .out(adder_43_out));  // open: cin, cout
  Adder #(.width(32)) adder_44 (.a(adder_43_out), .b(adder_45_out), .out(adder_44_out));  // open: cin, cout
  Adder #(.width(32)) adder_45 (
    .a(bit_extender_55_out), .b(bit_extender_56_out), .out(adder_45_out));  // open: cin, cout
  Adder #(.width(32)) adder_46 (
    .a(bit_extender_57_out), .b(bit_extender_58_out), .out(adder_46_out));  // open: cin, cout
  Adder #(.width(32)) adder_47 (.a(adder_46_out), .b(adder_48_out), .out(adder_47_out));  // open: cin, cout
  Adder #(.width(32)) adder_48 (
    .a(bit_extender_59_out), .b(bit_extender_60_out), .out(adder_48_out));  // open: cin, cout
  Adder #(.width(32)) adder_49 (
    .a(bit_extender_61_out), .b(bit_extender_62_out), .out(adder_49_out));  // open: cin, cout
  Adder #(.width(32)) adder_50 (.a(adder_49_out), .b(adder_51_out), .out(adder_50_out));  // open: cin, cout
  Adder #(.width(32)) adder_51 (
    .a(bit_extender_63_out), .b(bit_extender_64_out), .out(adder_51_out));  // open: cin, cout
  Adder #(.width(32)) adder_52 (
    .a(bit_extender_65_out), .b(bit_extender_66_out), .out(adder_52_out));  // open: cin, cout
  Adder #(.width(32)) adder_53 (.a(adder_52_out), .b(adder_54_out), .out(adder_53_out));  // open: cin, cout
  Adder #(.width(32)) adder_54 (
    .a(bit_extender_67_out), .b(bit_extender_68_out), .out(adder_54_out));  // open: cin, cout
  Adder #(.width(32)) adder_55 (.a(adder_27_out), .b(adder_28_out), .out(adder_55_out));  // open: cin, cout
  Adder #(.width(32)) adder_56 (.a(adder_29_out), .b(adder_30_out), .out(adder_56_out));  // open: cin, cout
  Adder #(.width(32)) adder_57 (.a(adder_32_out), .b(adder_35_out), .out(adder_57_out));  // open: cin, cout
  Adder #(.width(32)) adder_58 (.a(adder_38_out), .b(adder_41_out), .out(adder_58_out));  // open: cin, cout
  Adder #(.width(32)) adder_59 (.a(adder_44_out), .b(adder_47_out), .out(adder_59_out));  // open: cin, cout
  Adder #(.width(32)) adder_60 (.a(adder_50_out), .b(adder_53_out), .out(adder_60_out));  // open: cin, cout
  Adder #(.width(32)) adder_61 (.a(adder_55_out), .b(adder_56_out), .out(ontoB));  // open: cin, cout
  Adder #(.width(32)) adder_62 (.a(adder_57_out), .b(adder_58_out), .out(adder_62_out));  // open: cin, cout
  Adder #(.width(32)) adder_63 (.a(adder_59_out), .b(adder_60_out), .out(adder_63_out));  // open: cin, cout
  assign not_1_out = ~A;  // NOT_Gate not_1, 32 bits wide
  assign not_2_out = ~B;  // NOT_Gate not_2, 32 bits wide
  xor xor_2 (xor_2_out, B[31], A[31]);
  Adder #(.width(32)) adder_64 (.a(adder_62_out), .b(adder_63_out), .out(ontoA));  // open: cin, cout
  Adder #(.width(32)) adder_65 (.a(not_1_out), .b(32'h1), .out(adder_65_out));  // open: cin, cout
  Adder #(.width(32)) adder_66 (.a(not_2_out), .b(32'h1), .out(adder_66_out));  // open: cin, cout
  Multiplexer #(.width(32), .enable("false")) multiplexer_2 (
    .in0(A), .in1(adder_65_out), .out(multiplexer_2_out), .sel(A[31]));
  Multiplexer #(.width(32), .enable("false")) multiplexer_3 (
    .in0(B), .in1(adder_66_out), .out(multiplexer_3_out), .sel(B[31]));
  Multiplier #(.width(32)) multiplier_3 (
    .a(multiplexer_2_out), .b(multiplexer_3_out), .out(multiplier_3_out), .cout(multiplier_3_cout));  // open: cin
  Adder #(.width(32)) adder_67 (.a(32'h1), .b(multiplier_3_out), .cout(adder_67_cout));  // open: out, cin
  assign not_3_out = ~multiplier_3_cout;  // NOT_Gate not_3, 32 bits wide
  Multiplexer #(.width(32), .enable("false")) multiplexer_4 (
    .in0(multiplier_3_cout), .in1(adder_68_out), .out(mulh), .sel(xor_2_out));
  assign bit_extender_69_out = {{31{1'b0}}, adder_67_cout};  // Bit_Extender bit_extender_69
  Adder #(.width(32)) adder_68 (.a(bit_extender_69_out), .b(not_3_out), .out(adder_68_out));  // open: cin, cout

  // Other names for the same wires on the sheet: onto1 = A[0]; onto2 = A[1]; onto3 = A[2]; onto4 = A[3]; onto5 = A[4];
  //   onto6 = A[5]; onto7 = A[6]; onto8 = A[7]; onto9 = A[8]; onto10 = A[9]; onto11 = A[10]; onto12 = A[11];
  //   onto13 = A[12]; onto14 = A[13]; onto15 = A[14]; onto16 = A[15]; onto17 = A[16]; onto18 = A[17]; onto19 = A[18];
  //   onto20 = A[19]; onto21 = A[20]; onto22 = A[21]; onto23 = A[22]; onto24 = A[23]; onto25 = A[24]; onto26 = A[25];
  //   onto27 = A[26]; onto28 = A[27]; onto29 = A[28]; onto30 = A[29]; onto31 = A[30]; onto32 = A[31]; onto1B = B[0];
  //   onto2B = B[1]; onto3B = B[2]; onto4B = B[3]; onto5B = B[4]; onto6B = B[5]; onto7B = B[6]; onto8B = B[7];
  //   onto9B = B[8]; onto10B = B[9]; onto11B = B[10]; onto12B = B[11]; onto13B = B[12]; onto14B = B[13];
  //   onto15B = B[14]; onto16B = B[15]; onto17B = B[16]; onto18B = B[17]; onto19B = B[18]; onto20B = B[19];
  //   onto21B = B[20]; onto22B = B[21]; onto23B = B[22]; onto24B = B[23]; onto25B = B[24]; onto26B = B[25];
  //   onto27B = B[26]; onto28B = B[27]; onto29B = B[28]; onto30B = B[29]; onto31B = B[30]; onto32B = B[31]

  // Notes on the sheet:
  //   INPUTS to your circuit
  //   DON'T CHANGE THE LOCATIONS OF THE INPUTS AND OUTPUTS!
  //   OUTPUT from your circuit
endmodule
